# Fritzing sketch Projeto Integrador - Home Grow (saved by Fritzing 0.9.10b)
breadboards: 2

parts:
  MH-ET_LIVE_ESP32_DEVKIT1 = MH-ET LIVE ESP32 DEVKIT 38 pins
  DHT1 = DHT11 Humitidy and Temperature Sensor
  LED1 = smd LED [color="Green (570nm)" package="0805 [SMD]"]
  LED2 = smd LED [color="Yellow (595nm)" package="0805 [SMD]"]
  LED3 = smd LED [color="Red (633nm)" package="0805 [SMD]"]
  R1 = Resistor [tolerance=±5% resistance=220 package="0402 [SMD]"]
  R2 = Resistor [tolerance=±5% resistance=220 package="0402 [SMD]"]
  R3 = Resistor [tolerance=±5% resistance=220 package="0402 [SMD]"]
  R4 = Resistor [tolerance=±5% resistance=220 package="0402 [SMD]"]

nets:
  3V3: MH-ET_LIVE_ESP32_DEVKIT1.3V3, DHT1.VDD
  GND: MH-ET_LIVE_ESP32_DEVKIT1.GND, DHT1.GND, LED1.cathode, LED2.cathode, LED3.cathode
  N1: DHT1.DATA, R4.Pin_1
  N2: LED1.anode, R3.Pin_0
  N3: LED2.anode, R2.Pin_0
  N4: LED3.anode, R1.Pin_0

custom parts:
  MH-ET LIVE ESP32 DEVKIT 38 pins: http://mh.nodebb.com/topic/2/mh-et-live-esp32-devkit
  DHT11 Humitidy and Temperature Sensor: DHT11 Humidity and Temperature Sensor
